# Fritzing sketch calc (saved by Fritzing 0.9.6b)
circuit board: 10cm x 20cm

parts:
  S1 = Pushbutton [package="[THT]"]
  S2 = Pushbutton [package="[THT]"]
  S3 = Pushbutton [package="[THT]"]
  S4 = Pushbutton [package="[THT]"]
  S5 = Pushbutton [package="[THT]"]
  S6 = Pushbutton [package="[THT]"]
  S7 = Pushbutton [package="[THT]"]
  S8 = Pushbutton [package="[THT]"]
  S9 = Pushbutton [package="[THT]"]
  S10 = Pushbutton [package="[THT]"]
  S11 = Pushbutton [package="[THT]"]
  S12 = Pushbutton [package="[THT]"]
  S13 = Pushbutton [package="[THT]"]
  S14 = Pushbutton [package="[THT]"]
  S15 = Pushbutton [package="[THT]"]
  S16 = Pushbutton [package="[THT]"]
  J1 = male pin header, 4 pins [form="♂ (male)"]
  LED1 = RGB LED - (4 legs) [package="5 mm [THT]"]
  LED2 = RGB LED - (4 legs) [package="5 mm [THT]"]
  LED3 = RGB LED - (4 legs) [package="5 mm [THT]"]
  LED4 = RGB LED - (4 legs) [package="5 mm [THT]"]
  LED5 = RGB LED - (4 legs) [package="5 mm [THT]"]
  LED6 = RGB LED - (4 legs) [package="5 mm [THT]"]
  LED7 = RGB LED - (4 legs) [package="5 mm [THT]"]
  LED8 = RGB LED - (4 legs) [package="5 mm [THT]"]
  LED9 = RGB LED - (4 legs) [package="5 mm [THT]"]
  LED10 = RGB LED - (4 legs) [package="5 mm [THT]"]
  LED11 = RGB LED - (4 legs) [package="5 mm [THT]"]
  LED12 = RGB LED - (4 legs) [package="5 mm [THT]"]
  LED13 = RGB LED - (4 legs) [package="5 mm [THT]"]
  LED14 = RGB LED - (4 legs) [package="5 mm [THT]"]
  LED15 = RGB LED - (4 legs) [package="5 mm [THT]"]
  LED16 = RGB LED - (4 legs) [package="5 mm [THT]"]
  J2 = male pin header, 4 pins [form="♂ (male)"]
  J3 = male pin header, 4 pins [form="♂ (male)"]
  J4 = male pin header, 12 pins [form="♂ (male)"]

nets:
  N1: S1.Pin_1, S1.Pin_2, S5.Pin_1, S5.Pin_2, S9.Pin_1, S9.Pin_2, S13.Pin_1, S13.Pin_2, J3.pin1
  N2: S1.Pin_3, S1.Pin_4, S2.Pin_3, S2.Pin_4, S3.Pin_3, S3.Pin_4, S4.Pin_3, S4.Pin_4, J1.pin4
  N3: S2.Pin_1, S2.Pin_2, S6.Pin_1, S6.Pin_2, S10.Pin_1, S10.Pin_2, S14.Pin_1, S14.Pin_2, J3.pin2
  N4: S3.Pin_1, S3.Pin_2, S7.Pin_1, S7.Pin_2, S11.Pin_1, S11.Pin_2, S15.Pin_1, S15.Pin_2, J3.pin3
  N5: S4.Pin_1, S4.Pin_2, S8.Pin_1, S8.Pin_2, S12.Pin_1, S12.Pin_2, S16.Pin_1, S16.Pin_2, J3.pin4
  N6: S5.Pin_3, S5.Pin_4, S6.Pin_3, S6.Pin_4, S8.Pin_3, S8.Pin_4, J1.pin3
  N7: S7.Pin_3, S7.Pin_4
  N8: S9.Pin_3, S9.Pin_4, S10.Pin_3, S10.Pin_4, S11.Pin_3, S11.Pin_4, S12.Pin_3, S12.Pin_4, J1.pin2
  N9: S13.Pin_3, S13.Pin_4, S14.Pin_3, S14.Pin_4, S15.Pin_3, S15.Pin_4, S16.Pin_3, S16.Pin_4, J1.pin1
  N10: LED1.red_cathode, LED5.red_cathode, LED9.red_cathode, LED13.red_cathode, J4.pin1
  N11: LED1.common_anode, LED2.common_anode, LED3.common_anode, LED4.common_anode, J2.pin1
  N12: LED1.green_cathode, LED5.green_cathode, LED9.green_cathode, LED13.green_cathode, J4.pin2
  N13: LED1.blue_cathode, LED5.blue_cathode, LED9.blue_cathode, LED13.blue_cathode, J4.pin3
  N14: LED2.red_cathode, LED6.red_cathode, LED10.red_cathode, LED14.red_cathode, J4.pin4
  N15: LED2.green_cathode, LED6.green_cathode, LED10.green_cathode, LED14.green_cathode, J4.pin5
  N16: LED2.blue_cathode, LED6.blue_cathode, LED10.blue_cathode, LED14.blue_cathode, J4.pin6
  N17: LED3.red_cathode, LED7.red_cathode, LED11.red_cathode, LED15.red_cathode, J4.pin7
  N18: LED3.green_cathode, LED7.green_cathode, LED11.green_cathode, LED15.green_cathode, J4.pin8
  N19: LED3.blue_cathode, LED7.blue_cathode, LED11.blue_cathode, LED15.blue_cathode, J4.pin9
  N20: LED4.red_cathode, LED8.red_cathode, LED12.red_cathode, LED16.red_cathode, J4.pin10
  N21: LED4.green_cathode, LED8.green_cathode, LED12.green_cathode, LED16.green_cathode, J4.pin11
  N22: LED4.blue_cathode, LED8.blue_cathode, LED12.blue_cathode, LED16.blue_cathode, J4.pin12
  N23: LED5.common_anode, LED6.common_anode, LED7.common_anode, LED8.common_anode, J2.pin2
  N24: LED9.common_anode, LED10.common_anode, LED11.common_anode, LED12.common_anode, J2.pin3
  N25: LED13.common_anode, LED14.common_anode, LED15.common_anode, LED16.common_anode, J2.pin4
