# Fritzing sketch calc_guts (saved by Fritzing 0.9.6b)
circuit board: 6.5cm x 14.5cm

parts:
  GND = male pin header, 12 pins [form="♂ (male)"]
  IC1 = IC, DIP package, 6 pins [chip_label=IC]
  R2 = Resistor [tolerance=±5% power=0.25 resistance=33 package=THT]
  D1 = Rectifier Diode [part_number=1N4148 package="300 mil [THT]"]
  PICO = Raspberry Pi Pico
  4067_A = Analog Digital MUX Breakout
  4067_IN = male pin header, 16 pins [form="♂ (male)"]
  IN = MIDI_CONN_FEMALE_SUPPORT [package=din_5_female_support]
  THRU = MIDI_CONN_FEMALE_SUPPORT [package=din_5_female_support]
  OUT = MIDI_CONN_FEMALE_SUPPORT [package=din_5_female_support]
  J1 = Power Jack [package=power_jack_slot]
  D2 = Rectifier Diode [part_number=1N4001 package="300 mil [THT]"]
  C1 = Electrolytic Capacitor [capacitance=0.1mF voltage=35V package="100 mil [THT, electrolytic]"]
  U9 = 74HC595 [package="DIP16 [THT]"]
  U10 = 74HC595 [package="DIP16 [THT]"]
  RED = male pin header, 4 pins [form="♂ (male)"]
  GREEN = male pin header, 4 pins [form="♂ (male)"]
  BLUE = male pin header, 4 pins [form="♂ (male)"]
  COMMON = male pin header, 4 pins [form="♂ (male)"]
  Vcc = male pin header, 12 pins [form="♂ (male)"]
  J2 = male pin header, 2 pins [form="♂ (male)"]
  R1 = Resistor [tolerance=±5% power=0.25 resistance=10 package=THT]
  R3 = Resistor [tolerance=±5% power=0.25 resistance=470 package=THT]
  R4 = Resistor [tolerance=±5% power=0.25 resistance=220 package=THT]

nets:
  N1: GND.pin1, IC1.pin5, IN.NC1, THRU.NC1, OUT.NC1
  N2: GND.pin2, J1.GND, C1.-
  GND: GND.pin10, U9.GND, U9.OE, U10.GND, U10.OE
  N3: GND.pin11, 4067_A.GND
  N4: GND.pin12, PICO.pin_3, PICO.pin_38, PICO.pin_42
  N5: IC1.pin1, D1.cathode, R4.Pin_1
  N6: IC1.pin2, D1.anode, IN.MIDI_OUT, THRU.MIDI_OUT
  N7: IC1.pin4, PICO.pin_2, R3.Pin_1
  N8: IC1.pin6, R2.Pin_1, Vcc.pin1, R3.Pin_0
  N9: R2.Pin_0, OUT.MIDI_IN
  N10: PICO.pin_1, R1.Pin_1
  N11: PICO.pin_4, J2.pin1
  N12: PICO.pin_5, J2.pin2
  N13: PICO.pin_15, 4067_A.SIG
  N14: PICO.pin_16, 4067_A.S3
  N15: PICO.pin_17, 4067_A.S2
  N16: PICO.pin_19, 4067_A.S1
  N17: PICO.pin_20, 4067_A.S0
  N18: PICO.pin_22, U10.DS
  N19: PICO.pin_24, U9.SH_CP, U10.SH_CP
  N20: PICO.pin_25, U9.ST_CP, U10.ST_CP
  N21: 4067_A.C0, 4067_IN.pin16
  N22: 4067_A.C1, 4067_IN.pin15
  N23: 4067_A.C2, 4067_IN.pin14
  N24: 4067_A.C3, 4067_IN.pin13
  N25: 4067_A.C4, 4067_IN.pin12
  N26: 4067_A.C5, 4067_IN.pin11
  N27: 4067_A.C6, 4067_IN.pin10
  N28: 4067_A.C7, 4067_IN.pin9
  N29: 4067_A.C8, 4067_IN.pin8
  N30: 4067_A.C9, 4067_IN.pin7
  N31: 4067_A.C10, 4067_IN.pin6
  N32: 4067_A.C11, 4067_IN.pin5
  N33: 4067_A.C12, 4067_IN.pin4
  N34: 4067_A.C13, 4067_IN.pin3
  N35: 4067_A.C14, 4067_IN.pin2
  N36: 4067_A.C15, 4067_IN.pin1
  N37: IN.MIDI_IN, THRU.MIDI_IN, R4.Pin_0
  N38: OUT.MIDI_OUT, R1.Pin_0
  N39: J1.PWR, D2.anode
  N40: D2.cathode, C1.+
  N41: U9.Q1, COMMON.pin3
  N42: U9.Q2, COMMON.pin2
  N43: U9.Q3, COMMON.pin1
  N44: U9.Q4, BLUE.pin4
  N45: U9.Q5, BLUE.pin3
  N46: U9.Q6, BLUE.pin2
  N47: U9.Q7, BLUE.pin1
  VCC: U9.MR, U9.VCC, U10.MR, U10.VCC, Vcc.pin12
  N48: U9.DS, U10.Q7'
  N49: U9.Q0, COMMON.pin4
  N50: U10.Q1, GREEN.pin3
  N51: U10.Q2, GREEN.pin2
  N52: U10.Q3, GREEN.pin1
  N53: U10.Q4, RED.pin4
  N54: U10.Q5, RED.pin3
  N55: U10.Q6, RED.pin2
  N56: U10.Q7, RED.pin1
  N57: U10.Q0, GREEN.pin4

custom parts:
  Raspberry Pi Pico: Raspberry Pi Pico. Based around the RP2040 microcontroller the Pico is a low cost microcontroller device bringing Raspberry Pi quality, cost, and easy of use to the microcontroller space. Jan 2021, Split part in to two versions: tht (this one) and SMD. This one will drill holes for a .1 in header in pcb to allow plugging in the module as well as providing pads to solder the module to the top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
